// Logisim project FPA.circ as structural Verilog: 1 circuit, main circuit main
module main (
  input  [31:0] A,
  input  [31:0] B,
  output Overflow,
  output Underflow,
  output [31:0] Result
);

  wire ALU_carry_out, ALU_sign_bit, IPH_large_sign, IPH_small_sign, Normalizer_overflow, Rnd_out_3;
  wire [8:0] IPH_large_exp, Normalizer_normalized_exponent, RNor_changed_exponent;
  wire [31:0] ALU_result, IPH_l_significant, IPH_s_significant, Normalizer_normalized_significant,
       Rnd_rounded_significand;

  Input_Processing_Handler IPH (
    .A(A), .B(B), .L_significant(IPH_l_significant), .S_significant(IPH_s_significant),
    .LARGE_EXP(IPH_large_exp), .LARGE_SIGN(IPH_large_sign), .SMALL_SIGN(IPH_small_sign));  // open: Ea_nEb
  Significand_Adder ALU (
    .L_Sig(IPH_l_significant), .S_Sig(IPH_s_significant), .L_Sign(IPH_large_sign), .S_Sign(IPH_small_sign),
    .Result(ALU_result), .Carry_Out(ALU_carry_out), .Sign_Bit(ALU_sign_bit));
  Normalizer Normalizer (
    .Significand_input(ALU_result), .Exponent_Input(IPH_large_exp), .Carry(ALU_carry_out),
    .Normalized_Significant(Normalizer_normalized_significant),
    .Normalized_Exponent(Normalizer_normalized_exponent), .Overflow(Normalizer_overflow),
    .Underflow(Underflow));
  Rounder Rnd (
    .significand(Normalizer_normalized_significant), .rounded_significand(Rnd_rounded_significand),
    .out_3(Rnd_out_3));
  Rounded_Normalizer RNor (
    .Carry(Rnd_out_3), .Exponent(Normalizer_normalized_exponent), .Overflow(Normalizer_overflow),
    .Underflow(Underflow), .changed_Exponent(RNor_changed_exponent), .overflow_2(Overflow));
  // Output Repr: pin names not known; wires that end beside it: Rnd_rounded_significand, RNor_changed_exponent, ALU_sign_bit, Result
endmodule
